# Fritzing sketch Estacionamento_Esquematico (saved by Fritzing 0.9.6b)
perfboards: 2

parts:
  U3 = TCRT5000 [package=THT]
  R5 = Resistor [tolerance=±5% power=0.25 resistance=100 package=THT]
  R6 = Resistor [tolerance=±5% power=0.25 resistance=20k package=THT]
  U4 = TCRT5000 [package=THT]
  R7 = Resistor [tolerance=±5% power=0.25 resistance=100 package=THT]
  R8 = Resistor [tolerance=±5% power=0.25 resistance=20k package=THT]
  U5 = DC 5V TO ± 12V Mini DC converter [package=THT]
  SERVO1 = Tower Pro SG90 servo [part_number=101246]
  Componente1 = Arduino Nano (Rev3.0)
  VCC1 = Battery
  DI1 = 7-Segment LED Display [package=THT]
  R9 = Resistor [tolerance=±5% power=0.25 resistance=1k package=THT]
  S1 = Toggle Switch [package=THT]
  LED1 = LED - 3mm [color="Yellow (595nm)" current=0.030 package="3 mm [THT]"]
  LED2 = LED - 3mm [color="Red (633nm)" current=0.030 package="3 mm [THT]"]
  R10 = Resistor [tolerance=±5% power=0.25 resistance=1k package=THT]

nets:
  N1: U3.Pin_1, R6.Pin_1
  N2: U3.Pin_4, R5.Pin_0
  N3: R5.Pin_1, R6.Pin_0, R7.Pin_1, R8.Pin_0, Componente1.5V
  N4: U4.Pin_1, R8.Pin_1
  GND: U4.Pin_3, U5.+12V, SERVO1.GND, Componente1.GND, R10.Pin_1
  N5: U4.Pin_4, R7.Pin_0
  N6: U5.Vin, S1.COM
  N7: U5.GND, VCC1.-
  +5V: U5.-12V, SERVO1.+5V, Componente1.VIN, R9.Pin_0
  N8: SERVO1.Signal, Componente1.D11/MOSI
  N9: Componente1.D2, DI1.cathodeA, DI1.commAnode#7
  N10: Componente1.D3, DI1.cathodeB
  N11: Componente1.D4, DI1.cathodeC
  N12: Componente1.D5, DI1.cathodeD
  N13: Componente1.D6, DI1.cathodeE
  N14: Componente1.D7, DI1.cathodeF
  N15: Componente1.D8, DI1.cathodeG
  N16: Componente1.D10, LED2.cathode
  N17: Componente1.D12/MISO, LED1.anode
  N18: VCC1.+, S1.L1
  N19: DI1.commAnode#2, R9.Pin_1
  N20: LED1.cathode, LED2.anode, R10.Pin_0

custom parts:
  TCRT5000: TCRT5000 optical reflective sensor
  DC 5V TO ± 12V Mini DC converter: DC 5V TO ± 12V Mini DC converter from ebay (search for "DC 5V TO ± 12V Mini DC converter"). Supplies ± 12V at up to 30MA output for op amps or rs232 drivers from a 3 to 5V input (so a battery or 3.3 or 5V power rail) on a micro).
  Tower Pro SG90 servo: Original file by John De Cristofaro http://www.adafruit.com/products/1449 Adafruit Feedback Servo (Small) Edited by: e-radionica.com 28/9/2015
  Battery: Your standard 2x 18650 battery pack (7,4 Volts)
